# Fritzing sketch circuit_board (saved by Fritzing 0.9.5d)
circuit board: 3.82969cm x 3.82379cm
circuit board: 3.81351cm x 3.813cm

parts:
  U2 = 74AHCT125 [part_number=SN74AHCT125 package=dil14]  # not connected
  Yumo-enc4 = YumoE6B2  # not connected
  U3 = MMA_ACCEL_CONNECTOR [package=1x08]  # not connected
  U4 = MMA_ACCEL_CONNECTOR [package=1x08]  # not connected
  M5 = Stepper Motor - Bipolar  # not connected
  U5 = 74AHCT125 [part_number=SN74AHCT125 package=dil14]
  Yumo-enc5 = YumoE6B2
  U6 = MMA_ACCEL_CONNECTOR [package=1x08]
  U7 = MMA_ACCEL_CONNECTOR [package=1x08]
  M10 = Stepper Motor - Bipolar
  J1 = female pin header, 2 pins [form="♀ (female)"]
  J2 = female pin header, 2 pins [form="♀ (female)"]  # not connected
  J3 = female pin header, 2 pins [form="♀ (female)"]
  J4 = female pin header, 2 pins [form="♀ (female)"]  # not connected
  J5 = female pin header, 2 pins [form="♀ (female)"]  # not connected
  J6 = female pin header, 2 pins [form="♀ (female)"]  # not connected
  J7 = female pin header, 2 pins [form="♀ (female)"]  # not connected
  J8 = female pin header, 2 pins [form="♀ (female)"]  # not connected

nets:
  N1: U5.1OE, M10.D
  N2: U5.3Y, U5.4Y, M10.A, J3.pin1
  N3: U5.3OE, U6.Z
  N4: U5.4A, M10.C
  N5: U5.4OE, U6.GS2
  N6: Yumo-enc5.V, J1.pin2
  N7: Yumo-enc5.A, U7.X
  N8: Yumo-enc5.B, U7.Y
  N9: Yumo-enc5.Z, U7.Z
  N10: Yumo-enc5.GND, U7.GS1

notes:
  MH-ET Live ESP32
  CH9102X
  - - - - -

custom parts:
  74AHCT125: Quad Level-Shifter (3V to 5V) Quadruple Bus Buffer Gates With 3-State Outputs
