# Fritzing sketch main_circuit (saved by Fritzing 0.9.5d)

parts:
  Raspberry_Pi_4B = Raspberry Pi 4B
  MH-ET_Live_ESP32 = MH-ET Live Minikit for ESP32
  Power_plug2 = Power plug
  Power_plug3 = USB-C plug
  Power_plug4 = USB-C plug
  Power_plug5 = USB-C plug
  Power_plug6 = USB-C plug  # not connected
  USBTTL1 = USB A Plug  # not connected
  U1 = 74AHCT125 [part_number=SN74AHCT125 package=dil14]
  LED2 = WS2812 RGB LED strip
  LED1 = WS2812 RGB LED strip
  LED2_2 = WS2812 RGB LED strip
  LED1_2 = WS2812 RGB LED strip
  LED2_3 = WS2812 RGB LED strip
  LED1_3 = WS2812 RGB LED strip
  Power_plug_5v = Power plug

nets:
  GND: Raspberry_Pi_4B.GND, MH-ET_Live_ESP32.GND, U1.1OE, U1.2OE, U1.GND, LED2.GND#0, LED1.GND#0, Power_plug_5v.GND
  N1: Raspberry_Pi_4B.GPIO10, MH-ET_Live_ESP32.IO23
  N2: Raspberry_Pi_4B.GPIO11, MH-ET_Live_ESP32.IO18
  N3: Raspberry_Pi_4B.GPIO8, MH-ET_Live_ESP32.IO5
  N4: MH-ET_Live_ESP32.IO4, U1.2A
  N5: MH-ET_Live_ESP32.IO2, U1.1A
  GND_2: Power_plug2.GND, Power_plug5.GND
  VCC: Power_plug2.VCC, Power_plug5.VCC
  GND_3: Power_plug3.GND, Power_plug4.GND
  VCC_2: Power_plug3.VCC, Power_plug4.VCC
  N6: U1.1Y, LED1.DIN
  N7: U1.2Y, LED2.DIN
  VCC_3: U1.VCC, LED2.VCC#1, LED1.VCC#1, Power_plug_5v.VCC
  N8: LED2.GND#4, LED2_3.GND#0
  N9: LED2.VCC#5, LED2_3.VCC#1
  N10: LED2.DOUT, LED2_3.DIN
  N11: LED1.GND#4, LED1_3.GND#0
  N12: LED1.VCC#5, LED1_3.VCC#1
  N13: LED1.DOUT, LED1_3.DIN
  N14: LED2_2.GND, LED2_3.GND#4
  N15: LED2_2.VCC, LED2_3.VCC#5
  N16: LED2_2.DIN, LED2_3.DOUT
  N17: LED1_2.GND, LED1_3.GND#4
  N18: LED1_2.VCC, LED1_3.VCC#5
  N19: LED1_2.DIN, LED1_3.DOUT

notes:
  5 V
  MH-ET Live ESP32
  CH9102X
  Raspberry Pi4 2Gb
  - - - - -
  - - - - - - - - - - - - - - - - - - - - - -
  - -
  No connection
  WS2812B

custom parts:
  MH-ET Live Minikit for ESP32: MH-ET Live Minikit for ESP32 ( http://mh.nodebb.com/topic/8/mh-et-live-minikit-for-esp32/2/) PCB footprint is invalid.
  USB-C plug: power plug
  USB A Plug: USB A Plug breadboard only for documetnation purposes.
  74AHCT125: Quad Level-Shifter (3V to 5V) Quadruple Bus Buffer Gates With 3-State Outputs
  WS2812 RGB LED strip: WS2812 strip
