# Fritzing sketch circuit_board (saved by Fritzing 0.9.5d)
circuit board: 3.2131cm x 2.84892cm
circuit board: 3.2131cm x 2.84892cm

parts:
  J33 = female pin header, 2 pins [form="♀ (female)"]  # not connected
  M57 = Stepper Motor - Bipolar  # not connected
  M58 = Stepper Motor - Bipolar  # not connected
  M59 = Stepper Motor - Bipolar  # not connected
  S3 = Toggle Switch [package=THT]  # not connected
  IC3 = IC, DIP package, 8 pins [chip_label=IC]  # not connected
  ANT11 = Antenna  # not connected
  ANT12 = Antenna  # not connected
  M64 = Stepper Motor - Bipolar
  ANT13 = Antenna  # not connected
  ANT14 = Antenna  # not connected
  M65 = Stepper Motor - Bipolar
  IC7 = IC, DIP package, 8 pins [chip_label=IC]
  S7 = Toggle Switch [package=THT]
  J35 = female pin header, 2 pins [form="♀ (female)"]
  M66 = Stepper Motor - Bipolar
  Компонент1 = SMD Adapter  # not connected
  U11 = MCP7384XX [package=msop8]  # not connected
  C2 = Capacitor [package=0805]  # not connected
  R1 = Resistor [tolerance=±5% resistance=100 package="0805 [SMD]"]
  R2 = Resistor [tolerance=±5% resistance=100 package="0805 [SMD]"]
  C1 = Capacitor [package=0805]  # not connected

nets:
  N1: M64.A, IC7.pin1, IC7.pin8, S7.COM, M66.D
  N2: M64.C, M65.D
  N3: M64.B, M65.B
  N4: M64.D, M65.A
  N5: IC7.pin2, R2.Pin_0
  N6: IC7.pin3, R1.Pin_0
  N7: IC7.pin4, S7.L1, M66.A
  N8: IC7.pin5, S7.L2
  N9: IC7.pin6, J35.pin2
  N10: IC7.pin7, J35.pin1
  N11: M66.C, R1.Pin_1
  N12: M66.B, R2.Pin_1

notes:
  MH-ET Live ESP32
  CH9102X
  - - - - -

custom parts:
  SMD Adapter: SMD Adapter SO8 SOIC8 SOP
