# Fritzing sketch main_circuit (saved by Fritzing 0.9.5d)

parts:
  Power_plug2 = Power plug
  Power_plug5 = USB-C plug
  Power_plug6 = USB-C plug  # not connected
  LED2 = WS2812 RGB LED strip
  LED1 = WS2812 RGB LED strip
  LED2_2 = WS2812 RGB LED strip
  LED1_2 = WS2812 RGB LED strip
  LED2_3 = WS2812 RGB LED strip
  LED1_3 = WS2812 RGB LED strip
  Power_plug_5v = Power plug
  A1 = Waveshare rp2040-zero tht [package=THT]
  Raspberry_Pi_4B1 = Raspberry Pi 4B
  USBTTL1 = USB A Plug  # not connected
  R1 = Resistor [tolerance=±5% resistance=100 package="2512 [SMD]"]
  R2 = Resistor [tolerance=±5% resistance=100 package="2512 [SMD]"]
  C2 = Ceramic Capacitor [capacitance="100 nF" voltage=50V package="0603 [SMD, multilayer]"]
  C4 = Ceramic Capacitor [capacitance="100 nF" voltage=50V package="0603 [SMD, multilayer]"]
  U2 = LM358 [package=dip08]

nets:
  GND: Power_plug2.GND, Power_plug5.GND
  VCC: Power_plug2.VCC, Power_plug5.VCC
  GND_2: LED2.GND#0, LED1.GND#0, Power_plug_5v.GND, A1.Pin_2, Raspberry_Pi_4B1.GND, Raspberry_Pi_4B1.GPIO24, C2.1, C4.1, U2.G$1_V-, U2.G$2_+IN
  N1: LED2.VCC#1, LED1.VCC#1, Power_plug_5v.VCC, A1.Pin_1, C2.0, U2.G$1_OUT
  N2: LED2.DIN, R2.Pin_1
  N3: LED2.GND#4, LED2_3.GND#0
  N4: LED2.VCC#5, LED2_3.VCC#1
  N5: LED2.DOUT, LED2_3.DIN
  N6: LED1.DIN, R1.Pin_1
  N7: LED1.GND#4, LED1_3.GND#0
  N8: LED1.VCC#5, LED1_3.VCC#1
  N9: LED1.DOUT, LED1_3.DIN
  N10: LED2_2.GND, LED2_3.GND#4
  N11: LED2_2.VCC, LED2_3.VCC#5
  N12: LED2_2.DIN, LED2_3.DOUT
  N13: LED1_2.GND, LED1_3.GND#4
  N14: LED1_2.VCC, LED1_3.VCC#5
  N15: LED1_2.DIN, LED1_3.DOUT
  N16: A1.Pin_3, C4.0, U2.G$1_V+
  N17: A1.Pin_8, U2.G$2_OUT
  N18: A1.Pin_9, U2.G$2_-IN
  N19: A1.Pin_18, Raspberry_Pi_4B1.GPIO8, Raspberry_Pi_4B1.GPIO7, Raspberry_Pi_4B1.ID_SC
  N20: A1.Pin_19, Raspberry_Pi_4B1.3V3, Raspberry_Pi_4B1.GPIO10, Raspberry_Pi_4B1.GPIO9, Raspberry_Pi_4B1.GPIO25
  N21: A1.Pin_21, Raspberry_Pi_4B1.GPIO11
  N22: R1.Pin_0, U2.G$1_+IN
  N23: R2.Pin_0, U2.G$1_-IN

notes:
  5 V
  Pico rp2040
  Zero
  Raspberry Pi4 2Gb
  MH-ET Live ESP32
  CH9102X
  - - - - -
  - - - - - - - - - - - - - - - - - - - - - -
  - -
  No connection
  WS2812B
  SN74LVC2T45
  DCTR
  R1, R2
  100 Ohm
  100 nF
  C1, C2

custom parts:
  USB-C plug: power plug
  WS2812 RGB LED strip: WS2812 strip
  Waveshare rp2040-zero tht: .RP2040-Zero, A Low-Cost, High-Performance Pico-Like MCU Board Based On Raspberry Pi Microcontroller RP2040. This varant is THT without the extra connections.
